# Fritzing sketch semaforo (saved by Fritzing 0.9.3b)
breadboards: 1

parts:
  Componente1 = Arduino Uno (Rev3)
  R1 = Resistor [tolerance=±5% resistance=220 package=THT]
  R2 = Resistor [tolerance=±5% resistance=220 package=THT]
  R3 = Resistor [tolerance=±5% resistance=220 package=THT]
  R4 = Resistor [tolerance=±5% resistance=220 package=THT]
  R5 = Resistor [tolerance=±5% resistance=220 package=THT]
  LED1 = LED - 5mm [color="Green (555nm)" package="5 mm [THT]"]
  LED2 = LED - 5mm [color="Red (633nm)" package="5 mm [THT]"]
  LED3 = LED - 5mm [color="Yellow (585nm)" package="5 mm [THT]"]
  LED4 = LED - 5mm [color="Green (555nm)" package="5 mm [THT]"]
  LED5 = LED - 5mm [color="Red (633nm)" package="5 mm [THT]"]
  S3 = Pushbutton [package=THT]
  R6 = Rotary Potentiometer (Small) [maximum_resistance=10kΩ package=THT]
  R7 = Resistor [tolerance=±5% resistance=220 package=THT]

nets:
  N1: Componente1.A1, R6.wiper
  N2: Componente1.D8, S3.leg0, R7.Pin_0
  N3: Componente1.D2, R5.Pin_1
  N4: Componente1.D3_PWM, R4.Pin_1
  N5: Componente1.D4, R3.Pin_1
  N6: Componente1.D6_PWM, R2.Pin_1
  N7: Componente1.D7, R1.Pin_1
  N8: Componente1.5V, S3.leg1, R6.leg1
  N9: Componente1.GND, LED2.cathode, LED3.cathode, LED4.cathode, LED5.cathode, R6.leg2, R7.Pin_1
  N10: R1.Pin_0, LED1.anode
  N11: R2.Pin_0, LED5.anode
  N12: R3.Pin_0, LED2.anode
  N13: R4.Pin_0, LED3.anode
  N14: R5.Pin_0, LED4.anode
